# Fritzing sketch Lab1_extension1_devre (saved by Fritzing 0.9.3b)
breadboards: 1

parts:
  R1 = Resistor [tolerance=±5% resistance=220 package=THT]
  R2 = Resistor [tolerance=±5% resistance=220 package=THT]
  R3 = Resistor [tolerance=±5% resistance=220 package=THT]
  R4 = Resistor [tolerance=±5% resistance=220 package=THT]
  LED1 = smd LED [color="Red (633nm)" package="0603 [SMD]"]
  LED2 = smd LED [color="Red (633nm)" package="0603 [SMD]"]
  LED3 = smd LED [color="Red (633nm)" package="0603 [SMD]"]
  LED4 = smd LED [color="Red (633nm)" package="0603 [SMD]"]
  Parça1 = Arduino Uno (Rev3) - ICSP
  S1 = Momentary Switch [package=ksa_sealed_tac_switch]
  R5 = Resistor [tolerance=±5% resistance=220 package=THT]

nets:
  N1: R1.Pin_0, R2.Pin_0, R3.Pin_0, R4.Pin_0, Parça1.GND, R5.Pin_0
  N2: R1.Pin_1, LED1.cathode
  N3: R2.Pin_1, LED2.cathode
  N4: R3.Pin_1, LED3.cathode
  N5: R4.Pin_1, LED4.cathode
  N6: LED1.anode, Parça1.D5_PWM
  N7: LED2.anode, Parça1.D4
  N8: LED3.anode, Parça1.D3_PWM
  N9: LED4.anode, Parça1.D2
  N10: Parça1.D6_PWM, S1.3, R5.Pin_1
  N11: Parça1.3V3, S1.2
